# Fritzing sketch bmp085 (saved by Fritzing 0.8.7b)
breadboards: 1

parts:
  BMP085 = Barometric Pressure Sensor - BMP085 Breakout
  Atmega_/_Arduino = Arduino Ethernet Shield (Rev3)

nets:
  VCC: BMP085.VCC, Atmega_/_Arduino.3V3
  GND: BMP085.GND, Atmega_/_Arduino.GND
  N1: BMP085.SCL, Atmega_/_Arduino.A5/SCL
  N2: BMP085.SDA, Atmega_/_Arduino.A4/SDA
